# Fritzing sketch Arduino with SD card Reader, DHT11, LCD TMP36 (saved by Fritzing 0.9.3b)
circuit board: 8.46667cm x 5.64444cm
breadboards: 1

parts:
  LCM1602_IIC1 = LCM1602 IIC [part_number="LCM1602 IIC" chip_label="LCM1602 IIC" package="DIP (Dual Inline) [THT]"]
  LCD1 = LCD screen
  Part3 = Arduino Uno (Rev3)
  R4 = Resistor [tolerance=±5% resistance=330 package=THT]
  LED2 = LED - 5mm [color="Red (633nm)" package="5 mm [THT]"]
  Part4 = MicroSD Card Module
  RHT3 = Humidity and Temperature Sensor RHT03
  R5 = Resistor [tolerance=±5% resistance=10k package=THT]
  LED3 = LED - 5mm [color="Yellow (595nm)" package="5 mm [THT]"]
  R6 = Resistor [tolerance=±5% resistance=330 package=THT]
  LED4 = LED - 5mm [color="Green (570nm)" package="5 mm [THT]"]
  R7 = Resistor [tolerance=±5% resistance=330 package=THT]
  T1 = TMP36 Temperature Sensor [package="TO92 [THT]"]
  T2 = TMP36 Temperature Sensor [package="TO92 [THT]"]
  R8 = PHOTOCELL [package=photocell-kit]
  R9 = Resistor [tolerance=±5% resistance=10k package=THT]

nets:
  VSS: LCM1602_IIC1.VSS, LCD1.VSS
  VDD: LCM1602_IIC1.VDD, LCD1.VDD
  N1: LCM1602_IIC1.V0, LCD1.V0
  N2: LCM1602_IIC1.RS, LCD1.RS
  N3: LCM1602_IIC1.RW, LCD1.R/W
  N4: LCM1602_IIC1.E, LCD1.E
  N5: LCM1602_IIC1.D0, LCD1.DB0
  N6: LCM1602_IIC1.D1, LCD1.DB1
  N7: LCM1602_IIC1.D2, LCD1.DB2
  N8: LCM1602_IIC1.D3, LCD1.DB3
  N9: LCM1602_IIC1.D4, LCD1.DB4
  N10: LCM1602_IIC1.D5, LCD1.DB5
  N11: LCM1602_IIC1.D6, LCD1.DB6
  N12: LCM1602_IIC1.D7, LCD1.DB7
  N13: LCM1602_IIC1.A, LCD1.LED+
  N14: LCM1602_IIC1.K, LCD1.LED-
  N15: LCM1602_IIC1.SDA, Part3.A4/SDA
  N16: LCM1602_IIC1.SCL, Part3.A5/SCL
  N17: LCM1602_IIC1.LED_A, LCM1602_IIC1.LED_B
  N18: Part3.A0, T2.Vout
  N19: Part3.A1, T1.Vout
  N20: Part3.A2, R8.P$1, R9.Pin_1
  N21: Part3.D10_PWM/SS, Part4.CS
  N22: Part3.D11_PWM/MOSI, Part4.MOSI
  N23: Part3.D12/MISO, Part4.MISO
  N24: Part3.D13/SCK, Part4.SCK
  GND: Part3.GND, R4.Pin_0, Part4.GND, RHT3.GND_2, R7.Pin_0, T1.GND, T2.GND, R9.Pin_0
  N25: Part3.D2, RHT3.Data-signal, R5.Pin_1
  N26: Part3.D4, LED2.anode
  N27: Part3.D5_PWM, LED3.anode
  N28: Part3.D6_PWM, LED4.anode
  5V: Part3.5V, Part4.VCC
  N29: R4.Pin_1, LED2.cathode
  N30: RHT3.Vcc, R5.Pin_0
  N31: LED3.cathode, R6.Pin_1
  N32: LED4.cathode, R7.Pin_1
  N33: T1.+Vs, T2.+Vs, R8.P$2

custom parts:
  LCM1602 IIC: I2C-Module to use a 1602 or 2004 LCD on with the wire.h libory Serial LCD Modul

// code stored in the sketch: AnalogReadSerial2LCD_LED.ino
#include <Wire.h>
#include <LiquidCrystal_I2C.h>

LiquidCrystal_I2C lcd(0x27, 16, 2);   // adress and format LCD

const int analogInPin = A0;           // Analog input pin that the potentiometer is attached to
const int analogOutPin = 9;           // Analog output pin that the LED is attached to

int sensorValue = 0;                  // value read from the pot
int outputValue = 0;                  // value output to the PWM (analog out)

void setup() {
  lcd.init();                         // init LCD
  lcd.backlight();
  lcd.home();
  lcd.setCursor(5, 0);                // place static text
  lcd.print("ADC = ");
  lcd.setCursor(15, 0);
  lcd.print("V");
  lcd.setCursor(0, 1);
  lcd.print("LED : ");
  lcd.setCursor(12, 1);
  lcd.print("%");
  Serial.begin(9600);                 // optional serial monitor
}

void loop() {
  int sensorValue = analogRead(analogInPin);          // read analog A0 en store in sensorValue
  float voltValue = 5.0 / 1024.0 * sensorValue;       // calculate volt at analog A0 and store in voltValue
  float percentValue = sensorValue / 1024.0 * 100.0;  // calculate percentage analog A0 and store in percentValue
  outputValue = map(sensorValue, 0, 1023, 0, 255);    // map analog input to analog output and store in outputValue
  analogWrite(analogOutPin, outputValue);             // write outputValue to analogOutPin

  lcd.setCursor(0, 0);                                // set cursor at deserid position
  leadingZeros(sensorValue, 4);                       // print sensorvalue with number of leading-characters (0 or space as specified in function leadingZeros)
  lcd.setCursor(10, 0);                               // set cursor at deserid position
  lcd.print(voltValue);                               // print voltValue
  lcd.setCursor(6, 1);                                // set cursor at deserid position
  lcd.print(percentValue);                            // print percentValue

  Serial.print("sensor = " );                         // print the results to the serial monitor:
  Serial.print(sensorValue);
  Serial.print("\t output = ");
  Serial.print(outputValue);
  Serial.print("\t procent = ");
  Serial.println(percentValue);

  delay(1000);                                        // set delay
}

void leadingZeros( int value, int width) {            // display result with leading characters
  char valueStr[6];                                   // large enough to hold an int
  itoa (value, valueStr, 10);                         // itoa converts int to string
  int len = strlen(valueStr);                         // calculate length of valueStr
  if (len < width) {
    len = width - len;
    while (len--)
      lcd.print(' ');                                 // for leading zeros place '0' between (), for leading spaces place ' ' between ()
  }
  lcd.print(valueStr);
}
